# Fritzing sketch Diagrama TT (saved by Fritzing 0.9.3b)
breadboards: 1

parts:
  M1 = PH meter with sensor in breadboard [package=THT]  # not connected
  A1 = tds-sensor-meter-v1.0_1
  DS1 = DS18B20 1-Wire Temperature Sensor Probe  # not connected
  Espessif_Serial_Wifi_Modul_1 = ESP8266 ESP01 [part_number=ESP8266 package=THT]  # not connected
  A3 = Electical conductivity meter  # not connected
  A4 = TS 300B sensor  # not connected
  A5 = TS-300B interface  # not connected
  Componente1 = Arduino Mega ADK (Rev3)

nets:
  N1: A1.pin2, Componente1.5V
  N2: A1.pin3, Componente1.GND

custom parts:
  PH meter with sensor in breadboard: DFrobot PH meter (SKU SEN0161)
  : TDS Meter V1.0 Development Board Water Meter Filter Measuring Water Sensor Module.
  ESP8266 ESP01: Generic WiFi Module based on the ESP8266 with onboard PCB antenna and UART communications
  Electical conductivity meter: DFrobot Electrical conductivity meter (SKU DFR0300)
  TS 300B sensor: TS 300B water turbidity sensor.
  TS-300B interface: TS-300B interface.
