# Fritzing sketch Conexión ESP01, PRUEBA 1 (saved by Fritzing 0.9.3b)
breadboards: 1

parts:
  Componente1 = Arduino Mega ADK (Rev3)
  Espessif_Serial_Wifi_Modul_1 = ESP8266 ESP01 [part_number=ESP8266 package=THT]

nets:
  3V3: Componente1.3V3, Espessif_Serial_Wifi_Modul_1.VCC, Espessif_Serial_Wifi_Modul_1.CH_PD
  GND: Componente1.GND, Espessif_Serial_Wifi_Modul_1.GND, Espessif_Serial_Wifi_Modul_1.GPIO00, Espessif_Serial_Wifi_Modul_1.GPIO02
  N1: Componente1.D0/RX0, Espessif_Serial_Wifi_Modul_1.TXD
  N2: Componente1.D1/TX0, Espessif_Serial_Wifi_Modul_1.RXD

custom parts:
  ESP8266 ESP01: Generic WiFi Module based on the ESP8266 with onboard PCB antenna and UART communications
