# Fritzing sketch Prueba unitaria OD (saved by Fritzing 0.9.3b)

parts:
  Componente2 = Arduino Mega ADK (Rev3)
  A5 = Electical conductivity meter

nets:
  N1: Componente2.A0, A5.pin3
  N2: Componente2.5V, A5.pin2
  N3: Componente2.GND, A5.pin1

custom parts:
  Electical conductivity meter: DFrobot Electrical conductivity meter (SKU DFR0300)
