# Fritzing sketch Prueba unitaria TDS (saved by Fritzing 0.9.3b)
breadboards: 1

parts:
  Componente2 = Arduino Mega ADK (Rev3)
  A6 = tds-sensor-meter-v1.0_1

nets:
  N1: Componente2.A1, A6.pin1
  N2: Componente2.5V, A6.pin2
  N3: Componente2.GND, A6.pin3

custom parts:
  : TDS Meter V1.0 Development Board Water Meter Filter Measuring Water Sensor Module.
