# Fritzing sketch Prueba unitaria TSS (saved by Fritzing 0.9.3b)
breadboards: 1

parts:
  Componente2 = Arduino Mega ADK (Rev3)
  A7 = TS-300B interface
  A8 = TS 300B sensor

nets:
  N1: Componente2.A0, A7.Pin_2
  N2: Componente2.5V, A7.Pin_4
  N3: Componente2.GND, A7.Pin_1
  N4: A7.Pin_5, A8.Pin_1
  N5: A7.Pin_6, A8.Pin_2
  N6: A7.Pin_7, A8.Pin_3

custom parts:
  TS-300B interface: TS-300B interface.
  TS 300B sensor: TS 300B water turbidity sensor.
