# Fritzing sketch Prueba unitaria pH (saved by Fritzing 0.9.3b)

parts:
  Componente1 = Arduino Mega 2560 (Rev3)
  M1 = PH meter with sensor in breadboard [package=THT]

nets:
  N1: Componente1.A0, M1.pin1
  N2: Componente1.5V, M1.pin2
  N3: Componente1.GND, M1.pin3

custom parts:
  PH meter with sensor in breadboard: DFrobot PH meter (SKU SEN0161)
