# Fritzing sketch Prueba unitaria temperatura (saved by Fritzing 0.9.3b)

parts:
  Componente2 = Arduino Mega ADK (Rev3)
  DS2 = DS18B20 1-Wire Temperature Sensor Probe

nets:
  5V: Componente2.5V, DS2.VDD
  GND: Componente2.GND, DS2.GND
  N1: Componente2.D22, DS2.DQ
