# Fritzing sketch TT Moniroreo Esquemático (saved by Fritzing 0.9.3b)
circuit board: 8.46667cm x 5.64444cm
breadboards: 1

parts:
  M1 = PH meter with sensor in breadboard [package=THT]
  A1 = Electical conductivity meter
  DS1 = DS18B20 1-Wire Temperature Sensor Probe
  A2 = tds-sensor-meter-v1.0_1
  A3 = TS-300B interface
  A4 = TS 300B sensor
  Componente1 = Arduino Mega ADK (Rev3)
  Espessif_Serial_Wifi_Modul_1 = ESP8266 ESP01 [part_number=ESP8266 package=THT]

nets:
  N1: M1.pin1, Componente1.A2
  VDD: M1.pin2, A1.pin2, DS1.VDD, A2.pin2, A3.Pin_4, Componente1.5V
  GND: M1.pin3, A1.pin1, DS1.GND, A2.pin3, A3.Pin_1, Componente1.GND, Espessif_Serial_Wifi_Modul_1.GND
  N2: A1.pin3, Componente1.A3
  N3: A2.pin1, Componente1.A1
  N4: A3.Pin_2, Componente1.A0
  N5: A3.Pin_5, A4.Pin_1
  N6: A3.Pin_6, A4.Pin_2
  N7: A3.Pin_7, A4.Pin_3
  N8: Componente1.D19/RX1, Espessif_Serial_Wifi_Modul_1.TXD
  N9: Componente1.D18/TX1, Espessif_Serial_Wifi_Modul_1.RXD
  3V3: Componente1.3V3, Espessif_Serial_Wifi_Modul_1.VCC, Espessif_Serial_Wifi_Modul_1.CH_PD

custom parts:
  PH meter with sensor in breadboard: DFrobot PH meter (SKU SEN0161)
  Electical conductivity meter: DFrobot Electrical conductivity meter (SKU DFR0300)
  : TDS Meter V1.0 Development Board Water Meter Filter Measuring Water Sensor Module.
  TS-300B interface: TS-300B interface.
  TS 300B sensor: TS 300B water turbidity sensor.
  ESP8266 ESP01: Generic WiFi Module based on the ESP8266 with onboard PCB antenna and UART communications
