# Fritzing sketch r4 (saved by Fritzing 0.9.3b)
breadboards: 1

parts:
  A1 = Arduino Nano ESP32
  A2 = Arduino UNO R4 WiFi
  A3 = TS 300B sensor
  A4 = TS-300B interface
  A5 = PH meter
  M1 = PH meter with sensor in breadboard [package=THT]
  A6 = tds-sensor-meter-v1.0_1
  DS1 = DS18B20 1-Wire Temperature Sensor Probe

nets:
  N1: A1.Pin_2, A2.Pin_7
  N2: A1.Pin_14, A1.Pin_19, A2.Pin_9, A2.Pin_18, A2.Pin_25, A2.Pin_48, A4.Pin_1, A4.Pin_8, A5.pin1, M1.pin3, A6.pin3, DS1.GND
  N3: A2.Pin_8, A2.Pin_27, A4.Pin_4, A5.pin2, M1.pin2, A6.pin2, DS1.VDD
  N4: A2.Pin_12, M1.pin1
  N5: A2.Pin_13, A6.pin1
  N6: A2.Pin_15, A4.Pin_2
  N7: A2.Pin_36, DS1.DQ
  N8: A3.Pin_1, A4.Pin_7
  N9: A3.Pin_2, A4.Pin_6
  N10: A3.Pin_3, A4.Pin_5

custom parts:
  Arduino Nano ESP32: Arduino® Nano ESP32 tht.
  Arduino UNO R4 WiFi: The Arduino UNO R4 WiFi merges the RA4M1 microprocessor from Renesas with the ESP32-S3 from Espressif, creating an all-in-one tool for makers with enhanced processing power and a diverse array of new peripherals.
  TS 300B sensor: TS 300B water turbidity sensor.
  TS-300B interface: TS-300B interface.
  PH meter: DFrobot Dissolved Oxygen meter (SKU SEN0237A)
  PH meter with sensor in breadboard: DFrobot PH meter (SKU SEN0161)
  : TDS Meter V1.0 Development Board Water Meter Filter Measuring Water Sensor Module.
